// Logisim project Classlib.circ as structural Verilog: 16 circuits, main circuit HA_1
module HA_1 (
  input  A,
  input  B,
  output COUT__AB,
  output SUM__AB_prime__A_prime_B
);

  wire A_prime_B_out, AB_prime_out, not_1_out, not_2_out;

  not not_1 (not_1_out, B);
  not not_2 (not_2_out, A);
  and AB_prime (AB_prime_out, A, not_1_out);
  and A_prime_B (A_prime_B_out, not_2_out, B);
  and AB (COUT__AB, B, A);
  or or_1 (SUM__AB_prime__A_prime_B, AB_prime_out, A_prime_B_out);
endmodule

module FA_1 (
  input  A,
  input  Cin,
  input  B,
  output SUM,
  output Cout
);

  wire AB_out, XAB_out, XABC_out;

  and AB (AB_out, B, A);
  xor XAB (XAB_out, A, B);
  xor XABXC (SUM, Cin, XAB_out);
  and XABC (XABC_out, Cin, XAB_out);
  or or_1 (Cout, XABC_out, AB_out);
endmodule

module FA_4 (
  input  A0,
  input  A1,
  input  A2,
  input  A3,
  input  B0,
  input  B1,
  input  B2,
  input  B3,
  input  CIN,
  output S0,
  output S1,
  output S2,
  output S3,
  output COUT
);

  wire fa_1_1_cout, fa_1_2_cout, fa_1_3_cout;

  FA_1 fa_1_1 (.A(A0), .Cin(CIN), .B(B0), .SUM(S0), .Cout(fa_1_1_cout));
  FA_1 fa_1_2 (.A(A1), .Cin(fa_1_1_cout), .B(B1), .SUM(S1), .Cout(fa_1_2_cout));
  FA_1 fa_1_3 (.A(A2), .Cin(fa_1_2_cout), .B(B2), .SUM(S2), .Cout(fa_1_3_cout));
  FA_1 fa_1_4 (.A(A3), .Cin(fa_1_3_cout), .B(B3), .SUM(S3), .Cout(COUT));

  // Notes on the sheet:
  //   Full Adder
endmodule

// B
module INC_4 (
  input  CIN,
  input  A0,
  input  A1,
  input  A2,
  input  A3,
  output COUT,
  output S0,
  output S1,
  output S2,
  output S3
);

  wire ha_1_1_cout__ab, ha_1_2_cout__ab, ha_1_3_cout__ab;

  HA_1 ha_1_1 (.A(CIN), .B(A0), .COUT__AB(ha_1_1_cout__ab), .SUM__AB_prime__A_prime_B(S0));
  HA_1 ha_1_2 (.A(ha_1_1_cout__ab), .B(A1), .COUT__AB(ha_1_2_cout__ab), .SUM__AB_prime__A_prime_B(S1));
  HA_1 ha_1_3 (.A(ha_1_2_cout__ab), .B(A2), .COUT__AB(ha_1_3_cout__ab), .SUM__AB_prime__A_prime_B(S2));
  HA_1 ha_1_4 (.A(ha_1_3_cout__ab), .B(A3), .COUT__AB(COUT), .SUM__AB_prime__A_prime_B(S3));

  // Notes on the sheet:
  //   4-Bit Increment Schematic
endmodule

module Negate (
  input  PASS_prime_2_sCOMP,
  input  in_2,
  input  in_3,
  input  in_4,
  input  in_5,
  output out_6,
  output out_7,
  output out_8,
  output out_9,
  output out_10
);

  wire xor_1_out, xor_2_out, xor_3_out, xor_4_out;

  xor xor_1 (xor_1_out, PASS_prime_2_sCOMP, in_2);
  xor xor_2 (xor_2_out, PASS_prime_2_sCOMP, in_3);
  xor xor_3 (xor_3_out, PASS_prime_2_sCOMP, in_4);
  xor xor_4 (xor_4_out, PASS_prime_2_sCOMP, in_5);
  INC_4 inc_4_1 (
    .CIN(PASS_prime_2_sCOMP), .A0(xor_4_out), .A1(xor_3_out), .A2(xor_2_out), .A3(xor_1_out), .COUT(out_6),
    .S0(out_7), .S1(out_8), .S2(out_9), .S3(out_10));
endmodule

module MUX_1 (
  input  A,
  input  A_B_prime,
  input  B,
  output Y
);

  wire and_1_out, and_2_out, not_1_out;

  not not_1 (not_1_out, A_B_prime);
  and and_1 (and_1_out, A, A_B_prime);
  and and_2 (and_2_out, not_1_out, B);
  or or_1 (Y, and_1_out, and_2_out);
endmodule

module MUX_4 (
  input  S,
  input  A3,
  input  B3,
  input  A2,
  input  B2,
  input  A1,
  input  B1,
  input  A0,
  input  B0,
  output Y3,
  output Y2,
  output Y1,
  output Y0
);

  MUX_1 mux_1_1 (.A(A3), .A_B_prime(S), .B(B3), .Y(Y3));
  MUX_1 mux_1_2 (.A(A2), .A_B_prime(S), .B(B2), .Y(Y2));
  MUX_1 mux_1_3 (.A(A1), .A_B_prime(S), .B(B1), .Y(Y1));
  MUX_1 mux_1_4 (.A(A0), .A_B_prime(S), .B(B0), .Y(Y0));

  // Notes on the sheet:
  //   MUX_4 A/B' = 0, A = 12, B = 7
endmodule

module DEMUX_1 (
  input  I,
  input  S,
  output A,
  output B
);

  and and_1 (A, I, S);
  and and_2 (B, I, ~S);  // AND_Gate

  // Notes on the sheet:
  //   1-Bit Demultiplexer SOP Form
  //   I = IN
  //   S = Switch (A/B')
endmodule

module DEMUX_4 (
  input  D3,
  input  D2,
  input  D1,
  input  D0,
  input  A_B,
  output A3,
  output B3,
  output A2,
  output B2,
  output A1,
  output B1,
  output A0,
  output B0
);

  DEMUX_1 demux_1_1 (.S(A_B), .B(B3), .I(D3), .A(A3));
  DEMUX_1 demux_1_2 (.S(A_B), .B(B2), .I(D2), .A(A2));
  DEMUX_1 demux_1_3 (.S(A_B), .B(B1), .I(D1), .A(A1));
  DEMUX_1 demux_1_4 (.S(A_B), .B(B0), .I(D0), .A(A0));
endmodule

// ADD_SUB
module ADD_SUBT (
  input  Switch,
  input  B3,
  input  B2,
  input  B1,
  input  B0,
  input  A3,
  input  A2,
  input  A1,
  input  A0,
  output S3,
  output S2,
  output S1,
  output S0,
  output out_14
);

  wire inc_4_1_s0, inc_4_1_s1, inc_4_1_s2, inc_4_1_s3;
  wire [3:0] xor_4_out;

  Hex_Digit_Display hex_digit_display_1 (.value({B3, B2, B1, B0}));  // open: dp
  xor xor_1 (xor_4_out[3], Switch, B3);
  xor xor_2 (xor_4_out[2], Switch, B2);
  xor xor_3 (xor_4_out[1], Switch, B1);
  xor xor_4 (xor_4_out[0], Switch, B0);
  Hex_Digit_Display hex_digit_display_2 (.value(xor_4_out));  // open: dp
  Hex_Digit_Display hex_digit_display_3 (.value({A3, A2, A1, A0}));  // open: dp
  INC_4 inc_4_1 (
    .CIN(Switch), .A0(xor_4_out[0]), .A1(xor_4_out[1]), .A2(xor_4_out[2]), .A3(xor_4_out[3]),
    .S0(inc_4_1_s0), .S1(inc_4_1_s1), .S2(inc_4_1_s2), .S3(inc_4_1_s3));  // open: COUT
  FA_4 fa_4_1 (
    .CIN(1'b0), .A0(inc_4_1_s0), .A1(inc_4_1_s1), .B0(A0), .B1(A1), .A2(inc_4_1_s2), .B2(A2),
    .A3(inc_4_1_s3), .B3(A3), .S0(S0), .S1(S1), .S2(S2), .S3(S3), .COUT(out_14));
  Hex_Digit_Display hex_digit_display_4 (.value({S3, S2, S1, S0}));  // open: dp

  // Notes on the sheet:
  //   Switch = 1; Subtract, Switch = 0; Add
  //   Format goes X = A + B or A - B, order matters!
  //   If 1 = 0001, Bits go A3;A2:A1:A0
endmodule

module SHIFT (
  input  in_1,
  input  in_2,
  input  L_R_prime,
  input  SHNUM3,
  input  SHNUM2,
  input  SHNUM1,
  input  SHNUM0,
  output SHOUT3,
  output SHOUT2,
  output SHOUT1,
  output SHOUT0
);

  wire and_1_out, and_2_out, and_3_out, mux_4_4_y3, not_1_out, not_2_out, or_2_out;
  wire [0:0] mux_4_2_y0;
  wire [3:0] mux_4_1_y0, mux_4_3_y0, mux_4_4_y0, mux_4_5_y0, mux_4_6_y0;

  Hex_Digit_Display hex_digit_display_1 (.value({2'b00, in_1, in_2}));  // open: dp
  Hex_Digit_Display hex_digit_display_2 (.value({4{SHNUM0}}));  // open: dp
  and and_1 (and_1_out, in_2, not_1_out);
  not not_1 (not_1_out, in_1);
  not not_2 (not_2_out, in_2);
  and and_2 (and_2_out, not_2_out, in_1);
  and and_3 (and_3_out, in_1, in_2);
  Hex_Digit_Display hex_digit_display_3 (.value({4{SHNUM0}}));  // open: dp
  LED led_1 (.in(and_2_out));
  LED led_2 (.in(and_3_out));
  LED led_3 (.in(and_1_out));
  MUX_4 mux_4_1 (
    .A3(SHNUM0), .B3(SHNUM0), .A2(SHNUM0), .B2(SHNUM0), .A1(SHNUM0), .B1(SHNUM0), .A0(SHNUM0), .B0(SHNUM0),
    .Y3(mux_4_1_y0[3]), .Y2(mux_4_1_y0[3]), .Y1(mux_4_1_y0[3]), .Y0(mux_4_1_y0[0]), .S(or_2_out));
  MUX_4 mux_4_2 (
    .A3(1'b0), .B3(SHNUM0), .A2(SHNUM0), .B2(SHNUM0), .A1(SHNUM0), .B1(SHNUM0), .A0(SHNUM0), .B0(SHNUM0),
    .Y3(mux_4_1_y0[3]), .Y2(mux_4_1_y0[3]), .Y1(mux_4_1_y0[3]), .Y0(mux_4_2_y0[0]), .S(or_2_out));
  or or_1 (mux_4_1_y0[3], and_3_out, and_2_out);
  or or_2 (or_2_out, and_2_out, and_1_out, and_3_out);
  Hex_Digit_Display hex_digit_display_4 (.value({{3{mux_4_1_y0[3]}}, mux_4_1_y0[0]}));  // open: dp
  Hex_Digit_Display hex_digit_display_5 (.value({{3{mux_4_1_y0[3]}}, mux_4_2_y0[0]}));  // open: dp
  LED led_4 (.in(mux_4_1_y0[3]));
  LED led_5 (.in(and_3_out));
  LED led_6 (.in(or_2_out));
  MUX_4 mux_4_3 (
    .A3(mux_4_1_y0[3]), .B3(mux_4_1_y0[3]), .A2(mux_4_1_y0[3]), .B2(mux_4_1_y0[3]), .A1(mux_4_1_y0[0]),
    .B1(mux_4_1_y0[3]), .A0(1'b0), .B0(mux_4_1_y0[0]), .Y3(mux_4_3_y0[3]), .Y2(mux_4_3_y0[3]),
    .Y1(mux_4_3_y0[3]), .Y0(mux_4_3_y0[0]), .S(mux_4_1_y0[3]));
  MUX_4 mux_4_4 (
    .A3(1'b0), .B3(mux_4_1_y0[3]), .A2(mux_4_1_y0[3]), .B2(mux_4_1_y0[3]), .A1(mux_4_1_y0[3]),
    .B1(mux_4_1_y0[3]), .A0(mux_4_1_y0[3]), .B0(mux_4_2_y0[0]), .Y3(mux_4_4_y3), .Y2(mux_4_4_y0[3]),
    .Y1(mux_4_4_y0[1]), .Y0(mux_4_4_y0[0]), .S(mux_4_1_y0[3]));
  Hex_Digit_Display hex_digit_display_6 (.value({{3{mux_4_3_y0[3]}}, mux_4_3_y0[0]}));  // open: dp
  Hex_Digit_Display hex_digit_display_7 (.value({{2{mux_4_4_y0[3]}}, mux_4_4_y0[1:0]}));  // open: dp
  Hex_Digit_Display hex_digit_display_8 (.value({{2{mux_4_5_y0[3]}}, mux_4_5_y0[1:0]}));  // open: dp
  MUX_4 mux_4_5 (
    .A3(mux_4_3_y0[3]), .B3(mux_4_3_y0[3]), .A2(mux_4_3_y0[3]), .B2(mux_4_3_y0[3]), .A1(mux_4_3_y0[0]),
    .B1(mux_4_3_y0[3]), .A0(1'b0), .B0(mux_4_3_y0[0]), .Y3(mux_4_5_y0[3]), .Y2(mux_4_5_y0[3]),
    .Y1(mux_4_5_y0[1]), .Y0(mux_4_5_y0[0]), .S(and_3_out));
  MUX_4 mux_4_6 (
    .A3(1'b0), .B3(mux_4_4_y3), .A2(mux_4_4_y3), .B2(mux_4_4_y0[3]), .A1(mux_4_4_y0[3]), .B1(mux_4_4_y0[1]),
    .A0(mux_4_4_y0[1]), .B0(mux_4_4_y0[0]), .Y3(mux_4_6_y0[3]), .Y2(mux_4_6_y0[2]), .Y1(mux_4_6_y0[1]),
    .Y0(mux_4_6_y0[0]), .S(and_3_out));
  Hex_Digit_Display hex_digit_display_9 (.value(mux_4_6_y0));  // open: dp
  Hex_Digit_Display hex_digit_display_10 (.value({SHOUT3, SHOUT2, SHOUT1, SHOUT0}));  // open: dp
  MUX_4 mux_4_7 (
    .A3(mux_4_5_y0[3]), .B3(mux_4_6_y0[3]), .A2(mux_4_5_y0[3]), .B2(mux_4_6_y0[2]), .A1(mux_4_5_y0[1]),
    .B1(mux_4_6_y0[1]), .A0(mux_4_5_y0[0]), .B0(mux_4_6_y0[0]), .Y3(SHOUT3), .Y2(SHOUT2), .Y1(SHOUT1),
    .Y0(SHOUT0), .S(L_R_prime));

  assign SHNUM1 = SHNUM0;
  assign SHNUM2 = SHNUM0;
  assign SHNUM3 = SHNUM0;
  // also tied to GND on the sheet: SHNUM0

  // Notes on the sheet:
  //   Shift AMT
  //   1 = LEFT ; 0 = RIGHT
endmodule

module Multiply (
  input  A3,
  input  A2,
  input  A1,
  input  A0,
  input  B3,
  input  B2,
  input  B1,
  input  B0,
  output _2_7,
  output _2_6,
  output _2_5,
  output _2_4,
  output _2_3,
  output _2_2,
  output _2_1,
  output _2_0
);

  wire fa_4_1_s0, fa_4_1_s1, fa_4_1_s2, fa_4_1_s3, fa_4_2_s0, fa_4_2_s1, fa_4_2_s2, fa_4_2_s3, fa_4_3_cout,
       fa_4_3_s0, fa_4_3_s1, fa_4_3_s2, fa_4_3_s3, fa_4_4_s0, fa_4_4_s1, fa_4_4_s2, fa_4_4_s3, fa_4_5_cout,
       fa_4_5_s0, fa_4_5_s1, fa_4_5_s2, fa_4_5_s3, fa_4_6_s0, fa_4_6_s1, fa_4_6_s2, fa_4_6_s3, fa_4_7_cout,
       fa_4_7_s0, fa_4_7_s1, fa_4_7_s2, fa_4_7_s3, fa_4_9_cout, mux_4_6_y0, mux_4_6_y1, mux_4_6_y2,
       mux_4_6_y3, mux_4_7_y0, mux_4_7_y1, mux_4_7_y2, mux_4_7_y3, xor_1_out, xor_2_out, xor_3_out,
       xor_4_out, xor_5_out, xor_6_out, xor_7_out, xor_8_out, xor_9_out;
  wire [3:0] add_subt_1_s0, add_subt_2_s0, mux_4_1_y0, mux_4_2_y0, mux_4_3_y0, mux_4_4_y0, mux_4_5_y0;

  Hex_Digit_Display hex_digit_display_1 (.value({B3, B2, B1, B0}));  // open: dp
  Hex_Digit_Display hex_digit_display_2 (.value({A3, A2, A1, A0}));  // open: dp
  ADD_SUBT add_subt_1 (
    .Switch(A3), .B3(A3), .B2(A2), .B1(A1), .B0(A0), .A3(1'b0), .A2(1'b0), .A1(1'b0), .A0(1'b0),
    .S3(add_subt_1_s0[3]), .S2(add_subt_1_s0[2]), .S1(add_subt_1_s0[1]), .S0(add_subt_1_s0[0]));  // open: out_14
  ADD_SUBT add_subt_2 (
    .Switch(B3), .B3(B3), .B2(B2), .B1(B1), .B0(B0), .A3(1'b0), .A2(1'b0), .A1(1'b0), .A0(1'b0),
    .S3(add_subt_2_s0[3]), .S2(add_subt_2_s0[2]), .S1(add_subt_2_s0[1]), .S0(add_subt_2_s0[0]));  // open: out_14
  Hex_Digit_Display hex_digit_display_3 (.value(add_subt_1_s0));  // open: dp
  Hex_Digit_Display hex_digit_display_4 (.value(add_subt_2_s0));  // open: dp
  FA_4 fa_4_1 (
    .CIN(1'b0), .A0(1'b0), .A1(1'b0), .B0(add_subt_1_s0[0]), .B1(add_subt_1_s0[1]), .A2(1'b0),
    .B2(add_subt_1_s0[2]), .A3(1'b0), .B3(add_subt_1_s0[3]), .S0(fa_4_1_s0), .S1(fa_4_1_s1), .S2(fa_4_1_s2),
    .S3(fa_4_1_s3));  // open: COUT
  LED led_1 (.in(add_subt_2_s0[0]));
  MUX_4 mux_4_1 (
    .A3(fa_4_1_s3), .B3(1'b0), .A2(fa_4_1_s2), .B2(1'b0), .A1(fa_4_1_s1), .B1(1'b0), .A0(fa_4_1_s0),
    .B0(1'b0), .Y3(mux_4_1_y0[3]), .Y2(mux_4_1_y0[2]), .Y1(mux_4_1_y0[1]), .Y0(mux_4_1_y0[0]),
    .S(add_subt_2_s0[0]));
  FA_4 fa_4_2 (
    .CIN(fa_4_3_cout), .A0(1'b0), .A1(1'b0), .B0(add_subt_1_s0[3]), .B1(1'b0), .A2(1'b0), .B2(1'b0),
    .A3(1'b0), .B3(1'b0), .S0(fa_4_2_s0), .S1(fa_4_2_s1), .S2(fa_4_2_s2), .S3(fa_4_2_s3));  // open: COUT
  FA_4 fa_4_3 (
    .CIN(1'b0), .A0(mux_4_1_y0[0]), .A1(mux_4_1_y0[1]), .B0(1'b0), .B1(add_subt_1_s0[0]), .A2(mux_4_1_y0[2]),
    .B2(add_subt_1_s0[1]), .A3(mux_4_1_y0[3]), .B3(add_subt_1_s0[2]), .S0(fa_4_3_s0), .S1(fa_4_3_s1),
    .S2(fa_4_3_s2), .S3(fa_4_3_s3), .COUT(fa_4_3_cout));
  LED led_2 (.in(add_subt_2_s0[1]));
  MUX_4 mux_4_2 (
    .A3(fa_4_2_s3), .B3(1'b0), .A2(fa_4_2_s2), .B2(1'b0), .A1(fa_4_2_s1), .B1(1'b0), .A0(fa_4_2_s0),
    .B0(1'b0), .Y3(mux_4_2_y0[3]), .Y2(mux_4_2_y0[2]), .Y1(mux_4_2_y0[1]), .Y0(mux_4_2_y0[0]),
    .S(add_subt_2_s0[1]));
  MUX_4 mux_4_3 (
    .A3(fa_4_3_s3), .B3(mux_4_1_y0[3]), .A2(fa_4_3_s2), .B2(mux_4_1_y0[2]), .A1(fa_4_3_s1),
    .B1(mux_4_1_y0[1]), .A0(fa_4_3_s0), .B0(mux_4_1_y0[0]), .Y3(mux_4_3_y0[3]), .Y2(mux_4_3_y0[2]),
    .Y1(mux_4_3_y0[1]), .Y0(mux_4_3_y0[0]), .S(add_subt_2_s0[1]));
  Hex_Digit_Display hex_digit_display_5 (.value(mux_4_1_y0));  // open: dp
  FA_4 fa_4_4 (
    .CIN(fa_4_5_cout), .A0(mux_4_2_y0[0]), .A1(mux_4_2_y0[1]), .B0(add_subt_1_s0[2]), .B1(add_subt_1_s0[3]),
    .A2(mux_4_2_y0[2]), .B2(1'b0), .A3(mux_4_2_y0[3]), .B3(1'b0), .S0(fa_4_4_s0), .S1(fa_4_4_s1),
    .S2(fa_4_4_s2), .S3(fa_4_4_s3));  // open: COUT
  FA_4 fa_4_5 (
    .CIN(1'b0), .A0(mux_4_3_y0[0]), .A1(mux_4_3_y0[1]), .B0(1'b0), .B1(1'b0), .A2(mux_4_3_y0[2]),
    .B2(add_subt_1_s0[0]), .A3(mux_4_3_y0[3]), .B3(add_subt_1_s0[1]), .S0(fa_4_5_s0), .S1(fa_4_5_s1),
    .S2(fa_4_5_s2), .S3(fa_4_5_s3), .COUT(fa_4_5_cout));
  Hex_Digit_Display hex_digit_display_6 (.value(mux_4_2_y0));  // open: dp
  Hex_Digit_Display hex_digit_display_7 (.value(mux_4_3_y0));  // open: dp
  MUX_4 mux_4_4 (
    .A3(fa_4_4_s3), .B3(mux_4_2_y0[3]), .A2(fa_4_4_s2), .B2(mux_4_2_y0[2]), .A1(fa_4_4_s1),
    .B1(mux_4_2_y0[1]), .A0(fa_4_4_s0), .B0(mux_4_2_y0[0]), .Y3(mux_4_4_y0[3]), .Y2(mux_4_4_y0[2]),
    .Y1(mux_4_4_y0[1]), .Y0(mux_4_4_y0[0]), .S(add_subt_2_s0[2]));
  MUX_4 mux_4_5 (
    .A3(fa_4_5_s3), .B3(mux_4_3_y0[3]), .A2(fa_4_5_s2), .B2(mux_4_3_y0[2]), .A1(fa_4_5_s1),
    .B1(mux_4_3_y0[1]), .A0(fa_4_5_s0), .B0(mux_4_3_y0[0]), .Y3(mux_4_5_y0[3]), .Y2(mux_4_5_y0[2]),
    .Y1(mux_4_5_y0[1]), .Y0(mux_4_5_y0[0]), .S(add_subt_2_s0[2]));
  LED led_3 (.in(add_subt_2_s0[2]));
  FA_4 fa_4_6 (
    .CIN(fa_4_7_cout), .A0(mux_4_4_y0[0]), .A1(mux_4_4_y0[1]), .B0(add_subt_1_s0[1]), .B1(add_subt_1_s0[2]),
    .A2(mux_4_4_y0[2]), .B2(add_subt_1_s0[3]), .A3(mux_4_4_y0[3]), .B3(1'b0), .S0(fa_4_6_s0), .S1(fa_4_6_s1),
    .S2(fa_4_6_s2), .S3(fa_4_6_s3));  // open: COUT
  FA_4 fa_4_7 (
    .CIN(1'b0), .A0(mux_4_5_y0[0]), .A1(mux_4_5_y0[1]), .B0(1'b0), .B1(1'b0), .A2(mux_4_5_y0[2]), .B2(1'b0),
    .A3(mux_4_5_y0[3]), .B3(add_subt_1_s0[0]), .S0(fa_4_7_s0), .S1(fa_4_7_s1), .S2(fa_4_7_s2),
    .S3(fa_4_7_s3), .COUT(fa_4_7_cout));
  Hex_Digit_Display hex_digit_display_8 (.value(mux_4_4_y0));  // open: dp
  xor xor_1 (xor_1_out, A3, B3);
  MUX_4 mux_4_6 (
    .A3(fa_4_7_s3), .B3(mux_4_5_y0[3]), .A2(fa_4_7_s2), .B2(mux_4_5_y0[2]), .A1(fa_4_7_s1),
    .B1(mux_4_5_y0[1]), .A0(fa_4_7_s0), .B0(mux_4_5_y0[0]), .Y3(mux_4_6_y3), .Y2(mux_4_6_y2),
    .Y1(mux_4_6_y1), .Y0(mux_4_6_y0), .S(add_subt_2_s0[3]));
  Hex_Digit_Display hex_digit_display_9 (.value(mux_4_5_y0));  // open: dp
  MUX_4 mux_4_7 (
    .A3(fa_4_6_s3), .B3(mux_4_4_y0[3]), .A2(fa_4_6_s2), .B2(mux_4_4_y0[2]), .A1(fa_4_6_s1),
    .B1(mux_4_4_y0[1]), .A0(fa_4_6_s0), .B0(mux_4_4_y0[0]), .Y3(mux_4_7_y3), .Y2(mux_4_7_y2),
    .Y1(mux_4_7_y1), .Y0(mux_4_7_y0), .S(add_subt_2_s0[3]));
  LED led_4 (.in(add_subt_2_s0[3]));
  xor xor_2 (xor_2_out, xor_1_out, mux_4_7_y3);
  xor xor_3 (xor_3_out, xor_1_out, mux_4_7_y2);
  xor xor_4 (xor_4_out, xor_1_out, mux_4_7_y1);
  xor xor_5 (xor_5_out, xor_1_out, mux_4_7_y0);
  xor xor_6 (xor_6_out, xor_1_out, mux_4_6_y3);
  xor xor_7 (xor_7_out, xor_1_out, mux_4_6_y2);
  xor xor_8 (xor_8_out, xor_1_out, mux_4_6_y1);
  xor xor_9 (xor_9_out, xor_1_out, mux_4_6_y0);
  FA_4 fa_4_8 (
    .CIN(fa_4_9_cout), .A0(1'b0), .A1(1'b0), .B0(xor_5_out), .B1(xor_4_out), .A2(1'b0), .B2(xor_3_out),
    .A3(1'b0), .B3(xor_2_out), .S0(_2_4), .S1(_2_5), .S2(_2_6), .S3(_2_7));  // open: COUT
  FA_4 fa_4_9 (
    .CIN(xor_1_out), .A0(1'b0), .A1(1'b0), .B0(xor_9_out), .B1(xor_8_out), .A2(1'b0), .B2(xor_7_out),
    .A3(1'b0), .B3(xor_6_out), .S0(_2_0), .S1(_2_1), .S2(_2_2), .S3(_2_3), .COUT(fa_4_9_cout));
  Hex_Digit_Display hex_digit_display_10 (.value({_2_3, _2_2, _2_1, _2_0}));  // open: dp
  Hex_Digit_Display hex_digit_display_11 (.value({_2_7, _2_6, _2_5, _2_4}));  // open: dp

  // Notes on the sheet:
  //   X
  //   SOLN IN HEX
endmodule

module Divide (
  input  NUMB3,
  input  NUMB2,
  input  NUMB1,
  input  NUMB0,
  input  NUMT3,
  input  NUMT2,
  input  NUMT1,
  input  NUMT0,
  output QUO3,
  output QUO2,
  output QUO3_2,
  output QUO1,
  output QUO2_2,
  output QUO0,
  output QUO1_2,
  output QUO0_2
);

  wire add_subt_1_s0, add_subt_3_s0, add_subt_3_s1, add_subt_3_s2, add_subt_3_s3, add_subt_4_out_14,
       add_subt_5_s0, add_subt_5_s1, add_subt_5_s2, add_subt_5_s3, add_subt_7_out_14, add_subt_7_s0,
       add_subt_7_s1, add_subt_7_s2, add_subt_7_s3, add_subt_9_s0, add_subt_9_s1, add_subt_9_s2,
       add_subt_9_s3, mux_4_1_y0, mux_4_1_y1, mux_4_1_y2, mux_4_3_y0, mux_4_3_y1, mux_4_3_y2, mux_4_5_y0,
       mux_4_5_y1, mux_4_5_y2, nor_1_out, not_1_out, not_2_out, not_3_out, not_4_out, not_5_out, xor_1_out;
  wire [1:0] add_subt_2_s0;
  wire [3:0] mux_4_2_y0, mux_4_4_y0, mux_4_6_y0, or_1_out;

  Hex_Digit_Display hex_digit_display_1 (.value({NUMB3, NUMB2, NUMB1, NUMB0}));  // open: dp
  Hex_Digit_Display hex_digit_display_2 (.value({NUMT3, NUMT2, NUMT1, NUMT0}));  // open: dp
  LED led_1 (.in(NUMB3));
  LED led_2 (.in(NUMT3));
  ADD_SUBT add_subt_1 (
    .Switch(NUMB3), .B3(NUMB3), .B2(NUMB2), .B1(NUMB1), .B0(NUMB0), .A3(1'b0), .A2(1'b0), .A1(1'b0),
    .A0(1'b0), .S3(or_1_out[3]), .S2(or_1_out[2]), .S1(or_1_out[1]), .S0(add_subt_1_s0));  // open: out_14
  ADD_SUBT add_subt_2 (
    .Switch(NUMT3), .B3(NUMT3), .B2(NUMT2), .B1(NUMT1), .B0(NUMT0), .A3(1'b0), .A2(1'b0), .A1(1'b0),
    .A0(1'b0), .S3(mux_4_6_y0[2]), .S2(mux_4_6_y0[2]), .S1(add_subt_2_s0[1]), .S0(add_subt_2_s0[0]));  // open: out_14
  Hex_Digit_Display hex_digit_display_3 (.value(or_1_out));  // open: dp
  nor nor_1 (nor_1_out, or_1_out[3], or_1_out[2], or_1_out[1], add_subt_1_s0);
  Hex_Digit_Display hex_digit_display_4 (.value({{2{mux_4_6_y0[2]}}, add_subt_2_s0}));  // open: dp
  or or_1 (or_1_out[0], nor_1_out, add_subt_1_s0);
  ADD_SUBT add_subt_3 (
    .Switch(1'b1), .B3(or_1_out[3]), .B2(or_1_out[2]), .B1(or_1_out[1]), .B0(or_1_out[0]), .A3(1'b0),
    .A2(1'b0), .A1(1'b0), .A0(mux_4_6_y0[2]), .out_14(add_subt_2_s0[1]), .S3(add_subt_3_s3),
    .S2(add_subt_3_s2), .S1(add_subt_3_s1), .S0(add_subt_3_s0));
  ADD_SUBT add_subt_4 (
    .Switch(1'b1), .B3(or_1_out[3]), .B2(or_1_out[2]), .B1(or_1_out[1]), .B0(or_1_out[0]),
    .A3(mux_4_6_y0[2]), .A2(mux_4_6_y0[2]), .A1(add_subt_2_s0[1]), .A0(add_subt_2_s0[0]),
    .out_14(add_subt_4_out_14));  // open: S3, S2, S1, S0
  not not_1 (not_1_out, add_subt_2_s0[1]);
  not not_2 (not_2_out, add_subt_4_out_14);
  MUX_4 mux_4_1 (
    .A3(1'b0), .B3(add_subt_3_s3), .A2(1'b0), .B2(add_subt_3_s2), .A1(1'b0), .B1(add_subt_3_s1),
    .A0(mux_4_6_y0[2]), .B0(add_subt_3_s0), .Y2(mux_4_1_y2), .Y1(mux_4_1_y1), .Y0(mux_4_1_y0), .S(not_1_out));  // open: Y3
  MUX_4 mux_4_2 (
    .A3(1'b0), .B3(add_subt_2_s0[1]), .A2(1'b0), .B2(add_subt_2_s0[1]), .A1(1'b0), .B1(add_subt_7_out_14),
    .A0(1'b0), .B0(add_subt_2_s0[1]), .Y3(mux_4_2_y0[3]), .Y2(mux_4_2_y0[2]), .Y1(mux_4_2_y0[1]),
    .Y0(mux_4_2_y0[0]), .S(not_2_out));
  Hex_Digit_Display hex_digit_display_5 (.value(mux_4_2_y0));  // open: dp
  xor xor_1 (xor_1_out, NUMT3, NUMB3);
  ADD_SUBT add_subt_5 (
    .Switch(1'b1), .B3(or_1_out[3]), .B2(or_1_out[2]), .B1(or_1_out[1]), .B0(or_1_out[0]), .A3(mux_4_1_y2),
    .A2(mux_4_1_y1), .A1(mux_4_1_y0), .A0(mux_4_6_y0[2]), .out_14(add_subt_2_s0[1]), .S3(add_subt_5_s3),
    .S2(add_subt_5_s2), .S1(add_subt_5_s1), .S0(add_subt_5_s0));
  ADD_SUBT add_subt_6 (
    .Switch(xor_1_out), .B3(mux_4_2_y0[3]), .B2(mux_4_2_y0[2]), .B1(mux_4_2_y0[1]), .B0(mux_4_2_y0[0]),
    .A3(1'b0), .A2(1'b0), .A1(1'b0), .A0(1'b0), .S3(QUO3), .S2(QUO2), .S1(QUO1), .S0(QUO0));  // open: out_14
  not not_3 (not_3_out, add_subt_2_s0[1]);
  Hex_Digit_Display hex_digit_display_6 (.value({QUO3, QUO2, QUO1, QUO0}));  // open: dp
  MUX_4 mux_4_3 (
    .A3(mux_4_1_y2), .B3(add_subt_5_s3), .A2(mux_4_1_y1), .B2(add_subt_5_s2), .A1(mux_4_1_y0),
    .B1(add_subt_5_s1), .A0(mux_4_6_y0[2]), .B0(add_subt_5_s0), .Y2(mux_4_3_y2), .Y1(mux_4_3_y1),
    .Y0(mux_4_3_y0), .S(not_3_out));  // open: Y3
  ADD_SUBT add_subt_7 (
    .Switch(1'b1), .B3(or_1_out[3]), .B2(or_1_out[2]), .B1(or_1_out[1]), .B0(or_1_out[0]), .A3(mux_4_3_y2),
    .A2(mux_4_3_y1), .A1(mux_4_3_y0), .A0(add_subt_2_s0[1]), .out_14(add_subt_7_out_14), .S3(add_subt_7_s3),
    .S2(add_subt_7_s2), .S1(add_subt_7_s1), .S0(add_subt_7_s0));
  MUX_4 mux_4_4 (
    .A3(mux_4_6_y0[2]), .B3(mux_4_6_y0[3]), .A2(mux_4_6_y0[2]), .B2(mux_4_6_y0[2]), .A1(add_subt_2_s0[1]),
    .B1(mux_4_6_y0[1]), .A0(add_subt_2_s0[0]), .B0(mux_4_6_y0[0]), .Y3(mux_4_4_y0[3]), .Y2(mux_4_4_y0[2]),
    .Y1(mux_4_4_y0[1]), .Y0(mux_4_4_y0[0]), .S(not_2_out));
  Hex_Digit_Display hex_digit_display_7 (.value(mux_4_4_y0));  // open: dp
  not not_4 (not_4_out, add_subt_7_out_14);
  MUX_4 mux_4_5 (
    .A3(mux_4_3_y2), .B3(add_subt_7_s3), .A2(mux_4_3_y1), .B2(add_subt_7_s2), .A1(mux_4_3_y0),
    .B1(add_subt_7_s1), .A0(add_subt_2_s0[1]), .B0(add_subt_7_s0), .Y2(mux_4_5_y2), .Y1(mux_4_5_y1),
    .Y0(mux_4_5_y0), .S(not_4_out));  // open: Y3
  ADD_SUBT add_subt_8 (
    .Switch(xor_1_out), .B3(mux_4_4_y0[3]), .B2(mux_4_4_y0[2]), .B1(mux_4_4_y0[1]), .B0(mux_4_4_y0[0]),
    .A3(1'b0), .A2(1'b0), .A1(1'b0), .A0(1'b0), .S3(QUO3_2), .S2(QUO2_2), .S1(QUO1_2), .S0(QUO0_2));  // open: out_14
  Hex_Digit_Display hex_digit_display_8 (.value({QUO3_2, QUO2_2, QUO1_2, QUO0_2}));  // open: dp
  ADD_SUBT add_subt_9 (
    .Switch(1'b1), .B3(or_1_out[3]), .B2(or_1_out[2]), .B1(or_1_out[1]), .B0(or_1_out[0]), .A3(mux_4_5_y2),
    .A2(mux_4_5_y1), .A1(mux_4_5_y0), .A0(add_subt_2_s0[0]), .out_14(add_subt_2_s0[1]), .S3(add_subt_9_s3),
    .S2(add_subt_9_s2), .S1(add_subt_9_s1), .S0(add_subt_9_s0));
  not not_5 (not_5_out, add_subt_2_s0[1]);
  MUX_4 mux_4_6 (
    .A3(mux_4_5_y2), .B3(add_subt_9_s3), .A2(mux_4_5_y1), .B2(add_subt_9_s2), .A1(mux_4_5_y0),
    .B1(add_subt_9_s1), .A0(add_subt_2_s0[0]), .B0(add_subt_9_s0), .Y3(mux_4_6_y0[3]), .Y2(mux_4_6_y0[2]),
    .Y1(mux_4_6_y0[1]), .Y0(mux_4_6_y0[0]), .S(not_5_out));
  Hex_Digit_Display hex_digit_display_9 (.value(mux_4_6_y0));  // open: dp
endmodule

module ADD_SUBT_SYMBOL (
  input  B3,
  input  B3_2,
  input  B2,
  input  B2_2,
  input  B1,
  input  B1_2,
  input  B0,
  input  B0_2,
  input  Switch,
  input  Switch_2,
  input  A3,
  input  A3_2,
  input  A2,
  input  A2_2,
  input  A1,
  input  A1_2,
  input  A0,
  input  A0_2,
  output COUT,
  output S3,
  output S3_2,
  output S2,
  output S2_2,
  output S1,
  output S1_2,
  output S0,
  output S0_2,
  output S3_3,
  output S3_4,
  output S2_3,
  output S2_4,
  output S1_3,
  output S1_4,
  output S0_3,
  output S0_4
);

  ADD_SUBT add_subt_1 (
    .Switch(Switch), .B3(B3_2), .B2(B2_2), .B1(B1_2), .B0(B0_2), .A3(A3_2), .A2(A2_2), .A1(A1_2), .A0(A0_2),
    .out_14(COUT), .S3(S3_2), .S2(S2_2), .S1(S1_2), .S0(S0_2));
  Adder #(.width(4)) adder_1 (
    .a({B3_2, B2_2, B1_2, B0_2}), .b({A3_2, A2_2, A1_2, A0_2}), .out({S3_4, S2_4, S1_4, S0_4}));  // open: cin, cout
  Hex_Digit_Display hex_digit_display_1 (.value({B3_2, B2_2, B1_2, B0_2}));  // open: dp
  Hex_Digit_Display hex_digit_display_2 (.value({A3_2, A2_2, A1_2, A0_2}));  // open: dp
  Hex_Digit_Display hex_digit_display_3 (.value({S3_4, S2_4, S1_4, S0_4}));  // open: dp
  Hex_Digit_Display hex_digit_display_4 (.value({A3, A2, A1, A0}));  // open: dp
  ADD_SUBT add_subt_2 (
    .Switch(Switch_2), .B3(B3), .B2(B2), .B1(B1), .B0(B0), .A3(A3), .A2(A2), .A1(A1), .A0(A0), .S3(S3),
    .S2(S2), .S1(S1), .S0(S0));  // open: out_14
  Subtractor #(.width(4)) subtractor_1 (
    .a({A3, A2, A1, A0}), .b({B3, B2, B1, B0}), .out({S0_3, S1_3, S2_3, S3_3}));  // open: bin, bout
  Hex_Digit_Display hex_digit_display_5 (.value({B3, B2, B1, B0}));  // open: dp
  Hex_Digit_Display hex_digit_display_6 (.value({S0_3, S1_3, S2_3, S3_3}));  // open: dp

  // Notes on the sheet:
  //   MINE
  //   DEVICE SYMBOL
  //   +
  //   =
  //   Returns -14, but only represents the value as 4 bits. So, cuts off at the 4. 
  //   -
  //   =
endmodule

module SHIFT_TEST (
  input  S,
  input  [1:0] in_2,
  input  [3:0] in_3,
  output [3:0] out_4,
  output [3:0] out_5
);

  Shifter #(.width(4)) shifter_1 (.in(in_3), .\dist (in_2), .out(out_5));
  SHIFT shift_1 (
    .in_1(in_2[1]), .in_2(in_2[0]), .SHNUM3(in_3[3]), .SHNUM2(in_3[2]), .SHNUM1(in_3[1]), .SHNUM0(in_3[0]),
    .SHOUT3(out_4[3]), .SHOUT2(out_4[2]), .SHOUT1(out_4[1]), .SHOUT0(out_4[0]), .L_R_prime(S));

  // Notes on the sheet:
  //   Device Symbol
  //   My Circuit
endmodule

module MULT_TEST (
  input  [3:0] A,
  input  [3:0] B
);

  wire multiply_1_p3, multiply_1_p4, multiply_1_p5, multiply_1_p6, multiply_1_p7, multiply_1_p8,
       multiply_1_p9;

  // Multiply multiply_1: pin names not known; wires that end beside it: B[3], B[2], multiply_1_p3, multiply_1_p4, multiply_1_p5, multiply_1_p6, multiply_1_p7, multiply_1_p8, multiply_1_p9
endmodule
